// Logisim project PROJECT_LOGISIM.circ as structural Verilog: 1 circuit, main circuit main
module main (
  input  A,
  input  C,
  input  B,
  input  A_2,
  input  B_2,
  input  C_2,
  output F,
  output F_2
);

  wire and_1_out, and_2_out, and_3_out, nA_out, nand_1_out, nand_2_out, nand_3_out, nand_4_out, nand_5_out,
       nB_out, not_1_out, not_2_out, or_2_out;

  not not_1 (not_1_out, A);
  not not_2 (not_2_out, B);
  nand nA (nA_out, A_2, A_2);
  nand nB (nB_out, B_2, B_2);
  and and_1 (and_1_out, B, not_1_out);
  and and_2 (and_2_out, A, C);
  and and_3 (and_3_out, A, not_2_out);
  nand nand_1 (nand_1_out, nA_out, B_2);
  nand nand_2 (nand_2_out, nB_out, A_2);
  nand nand_3 (nand_3_out, A_2, C_2);
  or or_1 (F, and_1_out, or_2_out);
  or or_2 (or_2_out, and_2_out, and_3_out);
  nand nand_4 (nand_4_out, nand_1_out, nand_2_out);
  nand nand_5 (nand_5_out, nand_4_out, nand_4_out);
  nand nand_6 (F_2, nand_5_out, nand_3_out);

  // Notes on the sheet:
  //   AND-OR Circuit
  //   NAND Circuit
  //   F(A,B,C)=ABC+A’BC+AB’C’+AB’C+A’B’C
  //   A'B
  //   AC
  //   AB'
  //   AC+A'B
  //   (A'B)'
  //   (AB')'
  //   (AC)'
  //   A'B+AC+AB'
endmodule
